# Fritzing sketch stopwatch circuit (saved by Fritzing 0.9.3b)
breadboards: 1

parts:
  Part1 = Arduino Uno (Rev3)
  U1 = 74HC595 [package="DIP16 [THT]"]
  U2 = 74HC595 [package="DIP16 [THT]"]
  DI1 = 7-Segment LED Display [package=THT]
  DI2 = 7-Segment LED Display [package=THT]
  DI3 = 7-Segment LED Display [package=THT]
  DI4 = 7-Segment LED Display [package=THT]
  Q1 = NPN-Transistor [package="TO92 [THT]"]
  Q2 = NPN-Transistor [package="TO92 [THT]"]
  Q3 = NPN-Transistor [package="TO92 [THT]"]
  Q4 = NPN-Transistor [package="TO92 [THT]"]
  R1 = Resistor [tolerance=±5% resistance=10k package="1206 [SMD]"]
  R2 = Resistor [tolerance=±5% resistance=10k package="1206 [SMD]"]
  R3 = Resistor [tolerance=±5% resistance=10k package="1206 [SMD]"]
  R4 = Resistor [tolerance=±5% resistance=10k package="1206 [SMD]"]
  R5 = Resistor [tolerance=±5% resistance=220 package="0402 [SMD]"]
  R6 = Resistor [tolerance=±5% resistance=220 package="0402 [SMD]"]
  R7 = Resistor [tolerance=±5% resistance=220 package="0402 [SMD]"]
  R8 = Resistor [tolerance=±5% resistance=220 package="0402 [SMD]"]
  R9 = Resistor [tolerance=±5% resistance=220 package="0402 [SMD]"]
  R10 = Resistor [tolerance=±5% resistance=220 package="0402 [SMD]"]
  R11 = Resistor [tolerance=±5% resistance=220 package="0402 [SMD]"]
  R12 = Resistor [tolerance=±5% resistance=220 package="0402 [SMD]"]

nets:
  N1: Part1.D8, U1.ST_CP, U2.ST_CP
  N2: Part1.D9_PWM, U1.SH_CP, U2.SH_CP
  N3: Part1.D10_PWM/SS, U1.DS
  VCC: Part1.5V, U1.MR, U1.VCC, U2.MR, U2.VCC
  GND: Part1.GND, U1.GND, U1.OE, U2.GND, U2.OE, Q1.B, Q2.B, Q3.B, Q4.B, R1.Pin_0, R2.Pin_0, R3.Pin_0, R4.Pin_0
  N4: U1.Q1, R5.Pin_1
  N5: U1.Q2, R6.Pin_1
  N6: U1.Q3, R7.Pin_1
  N7: U1.Q4, R8.Pin_1
  N8: U1.Q5, R9.Pin_1
  N9: U1.Q6, R10.Pin_1
  N10: U1.Q7, R11.Pin_1
  N11: U1.Q7', U2.DS
  N12: U1.Q0, R12.Pin_0
  N13: U2.Q1, R2.Pin_1
  N14: U2.Q2, R3.Pin_1
  N15: U2.Q3, R4.Pin_1
  N16: U2.Q0, R1.Pin_1
  N17: DI1.cathodeE, DI2.cathodeE, DI3.cathodeE, DI4.cathodeE, R5.Pin_0
  N18: DI1.cathodeD, DI2.cathodeD, R12.Pin_1
  N19: DI1.cathodeC, DI2.cathodeC, DI3.cathodeC, DI4.cathodeC, R9.Pin_0
  N20: DI1.cathodeDP, DI2.cathodeDP, DI3.cathodeDP, DI4.cathodeDP, R10.Pin_0
  N21: DI1.cathodeB, DI2.cathodeB, DI3.cathodeB, DI4.cathodeB, R8.Pin_0
  N22: DI1.cathodeA, DI2.cathodeA, DI3.cathodeA, DI4.cathodeA, R7.Pin_0
  N23: DI1.commAnode#7, Q4.C
  N24: DI1.cathodeF, DI2.cathodeF, DI3.cathodeF, DI4.cathodeF, R6.Pin_0
  N25: DI1.cathodeG, DI2.cathodeG, DI3.cathodeG, DI4.cathodeG, R11.Pin_0
  N26: DI2.commAnode#7, Q3.C
  N27: DI3.cathodeD, DI4.cathodeD
  N28: DI3.commAnode#7, Q2.C
  N29: DI4.commAnode#7, Q1.C
